# Fritzing sketch VigiEsquematico (saved by Fritzing 0.9.6b)
breadboards: 1

parts:
  R10 = Resistor [tolerance=±5% resistance=1k package="0402 [SMD]"]
  R11 = Resistor [tolerance=±5% resistance=2.2k package="0402 [SMD]"]
  Rasp_5 = Raspberry Pi 4B
  J1 = JST-B3P-VH [part_number="Sensor E18-D80NK" package=THT]

nets:
  N1: R10.Pin_0, J1.pin3
  N2: R10.Pin_1, R11.Pin_0, Rasp_5.GPIO17
  N3: R11.Pin_1, Rasp_5.GND, J1.pin2
  N4: Rasp_5.5V, J1.pin1

notes:
  Camera RPi Cam não inclusa no Fritzing
